# Fritzing sketch trixie-digital-gauge (saved by Fritzing 0.9.3b)

parts:
  Part2 = OLED Color 1.5 inch 128x128 w microSD [part_number=1431]
  MCU1 = Raspberry Pi Zero
  ENCODER1 = Rotary Encoder with Knob

nets:
  N1: Part2.MOSI, MCU1.pin_19
  N2: Part2.SCK, MCU1.pin_23
  N3: MCU1.pin_25, MCU1.pin_39, ENCODER1.no_name_yet#3, ENCODER1.no_name_yet#4
  N4: MCU1.pin_33, ENCODER1.no_name_yet#1
  N5: MCU1.pin_35, ENCODER1.no_name_yet#2
  N6: MCU1.pin_37, ENCODER1.no_name_yet#5

custom parts:
  OLED Color 1.5 inch 128x128 w microSD: The visible portion of this OLED measures 1.5" diagonal and contains 128x128 RGB pixels, each one made of red, green and blue OLEDs. Each pixel can be set with 16-bits of resolution for a large range of colors. Because the display uses OLEDs, there is no backlight, and the contrast is very high (black is really black). We picked this display for its excellent color, this is the nicest mini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
  Rotary Encoder with Knob: Rotary Encoder with 1/4" Shaft and Knob
